// Logisim project cpu.circ as structural Verilog: 13 circuits, main circuit main
module main (
  input  in_1,
  output [31:0] out_2,
  output out_3,
  output [4:0] out_4,
  output [31:0] out_5,
  output out_6,
  output [4:0] out_7,
  output [31:0] out_8
);

  wire clk, DM_awake, IsignPC, JsignPC, RsignPC;
  wire [15:0] Iimm;
  wire [31:0] CalNumA, CalNumB, DM_RD, Jadd, PC, Rrs;

  Clock clock_1 (.out(clk));
  IFU ifu_1 (
    .clk(clk), .reset(in_1), .RsignPC(RsignPC), .IsignPC(IsignPC), .JsignPC(JsignPC), .Rrs(Rrs), .Iimm(Iimm),
    .Jadd(Jadd), .instr(out_2), .PC(PC));
  RF_controller rf_controller_1 (
    .clk(clk), .reset(in_1), .RD1(CalNumA), .RD2(CalNumB), .WD(out_5), .Instr(out_2), .RF_WE(out_3),
    .RF_Add(out_4), .PC(PC));
  ALU alu_1 (
    .A(CalNumA), .B(CalNumB), .Instr(out_2), .Result(out_5), .DM_WE(out_6), .DM_A(out_7), .DM_WD(out_8),
    .DM_RD(DM_RD), .RsignPC(RsignPC), .limm(Iimm), .DM_awake(DM_awake), .Rrs(Rrs), .Jadd(Jadd),
    .IsignPC(IsignPC), .JsignPC(JsignPC));
  DM dm_1 (.clk(clk), .reset(in_1), .WE(out_6), .A(out_7), .WD(out_8), .DM_awake(DM_awake), .RD(DM_RD));

  // Other names for the same wires on the sheet: Instr[31:0] = out_2; DM_A[4:0] = out_7; MemAddr[4:0] = out_7;
  //   DM_WD[31:0] = out_8; MemData[31:0] = out_8; DM_WE = out_6; MemWrite = out_6; RegAddr[4:0] = out_4;
  //   RF_Add[4:0] = out_4; RegData[31:0] = out_5; RF_WD[31:0] = out_5; RegWrite = out_3; RF_WE = out_3; Reset = in_1
endmodule

module RF (
  input  clk,
  input  reset,
  input  WE,
  input  [4:0] A1,
  input  [4:0] A2,
  input  [4:0] A3,
  input  [31:0] WD,
  output [31:0] RD1,
  output [31:0] RD2
);

  wire [31:0] in00, in01, in02, in03, in04, in05, in06, in07, in08, in09, in10, in11, in12, in13, in14, in15,
       in16, in17, in18, in19, in20, in21, in22, in23, in24, in25, in26, in27, in28, in29, in30, in31, out00,
       out01, out02, out03, out04, out05, out06, out07, out08, out09, out10, out11, out12, out13, out14,
       out15, out16, out17, out18, out19, out20, out21, out22, out23, out24, out25, out26, out27, out28,
       out29, out30, out31;

  // Probe on WD
  Demultiplexer #(.select(5), .width(32), .tristate("true"), .enable("false")) demultiplexer_1 (
    .out0(in00), .out1(in01), .out2(in02), .out3(in03), .out4(in04), .out5(in05), .out6(in06), .out7(in07),
    .out8(in08), .out9(in09), .out10(in10), .out11(in11), .out12(in12), .out13(in13), .out14(in14),
    .out15(in15), .out16(in16), .out17(in17), .out18(in18), .out19(in19), .out20(in20), .out21(in21),
    .out22(in22), .out23(in23), .out24(in24), .out25(in25), .out26(in26), .out27(in27), .out28(in28),
    .out29(in29), .out30(in30), .out31(in31), .in(WD), .sel(A3));
  // Probe on A3
  Register #(.width(32)) register_1 (.D(in00), .Q(out00), .clr(1'b1));  // open: en, clk
  Register #(.width(32)) register_2 (.D(in08), .en(WE), .Q(out08), .clk(clk), .clr(reset));
  Register #(.width(32)) register_3 (.D(in16), .en(WE), .Q(out16), .clk(clk), .clr(reset));
  Register #(.width(32)) register_4 (.D(in24), .en(WE), .Q(out24), .clk(clk), .clr(reset));
  Register #(.width(32)) register_5 (.D(in01), .en(WE), .Q(out01), .clk(clk), .clr(reset));
  Register #(.width(32)) register_6 (.D(in09), .en(WE), .Q(out09), .clk(clk), .clr(reset));
  Register #(.width(32)) register_7 (.D(in17), .en(WE), .Q(out17), .clk(clk), .clr(reset));
  Register #(.width(32)) register_8 (.D(in25), .en(WE), .Q(out25), .clk(clk), .clr(reset));
  Multiplexer #(.select(5), .width(32), .enable("false")) multiplexer_1 (
    .in0(out00), .in1(out01), .in2(out02), .in3(out03), .in4(out04), .in5(out05), .in6(out06), .in7(out07),
    .in8(out08), .in9(out09), .in10(out10), .in11(out11), .in12(out12), .in13(out13), .in14(out14),
    .in15(out15), .in16(out16), .in17(out17), .in18(out18), .in19(out19), .in20(out20), .in21(out21),
    .in22(out22), .in23(out23), .in24(out24), .in25(out25), .in26(out26), .in27(out27), .in28(out28),
    .in29(out29), .in30(out30), .in31(out31), .out(RD1), .sel(A1));
  Register #(.width(32)) register_9 (.D(in02), .en(WE), .Q(out02), .clk(clk), .clr(reset));
  Register #(.width(32)) register_10 (.D(in10), .en(WE), .Q(out10), .clk(clk), .clr(reset));
  Register #(.width(32)) register_11 (.D(in18), .en(WE), .Q(out18), .clk(clk), .clr(reset));
  Register #(.width(32)) register_12 (.D(in26), .en(WE), .Q(out26), .clk(clk), .clr(reset));
  Register #(.width(32)) register_13 (.D(in03), .en(WE), .Q(out03), .clk(clk), .clr(reset));
  Register #(.width(32)) register_14 (.D(in11), .en(WE), .Q(out11), .clk(clk), .clr(reset));
  Register #(.width(32)) register_15 (.D(in19), .en(WE), .Q(out19), .clk(clk), .clr(reset));
  Register #(.width(32)) register_16 (.D(in27), .en(WE), .Q(out27), .clk(clk), .clr(reset));
  Register #(.width(32)) register_17 (.D(in04), .en(WE), .Q(out04), .clk(clk), .clr(reset));
  Register #(.width(32)) register_18 (.D(in12), .en(WE), .Q(out12), .clk(clk), .clr(reset));
  Register #(.width(32)) register_19 (.D(in20), .en(WE), .Q(out20), .clk(clk), .clr(reset));
  Register #(.width(32)) register_20 (.D(in28), .en(WE), .Q(out28), .clk(clk), .clr(reset));
  Multiplexer #(.select(5), .width(32), .enable("false")) multiplexer_2 (
    .in0(out00), .in1(out01), .in2(out02), .in3(out03), .in4(out04), .in5(out05), .in6(out06), .in7(out07),
    .in8(out08), .in9(out09), .in10(out10), .in11(out11), .in12(out12), .in13(out13), .in14(out14),
    .in15(out15), .in16(out16), .in17(out17), .in18(out18), .in19(out19), .in20(out20), .in21(out21),
    .in22(out22), .in23(out23), .in24(out24), .in25(out25), .in26(out26), .in27(out27), .in28(out28),
    .in29(out29), .in30(out30), .in31(out31), .out(RD2), .sel(A2));
  Register #(.width(32)) register_21 (.D(in05), .en(WE), .Q(out05), .clk(clk), .clr(reset));
  Register #(.width(32)) register_22 (.D(in13), .en(WE), .Q(out13), .clk(clk), .clr(reset));
  Register #(.width(32)) register_23 (.D(in21), .en(WE), .Q(out21), .clk(clk), .clr(reset));
  Register #(.width(32)) register_24 (.D(in29), .en(WE), .Q(out29), .clk(clk), .clr(reset));
  Register #(.width(32)) register_25 (.D(in06), .en(WE), .Q(out06), .clk(clk), .clr(reset));
  Register #(.width(32)) register_26 (.D(in14), .en(WE), .Q(out14), .clk(clk), .clr(reset));
  Register #(.width(32)) register_27 (.D(in22), .en(WE), .Q(out22), .clk(clk), .clr(reset));
  Register #(.width(32)) register_28 (.D(in30), .en(WE), .Q(out30), .clk(clk), .clr(reset));
  Register #(.width(32)) register_29 (.D(in07), .en(WE), .Q(out07), .clk(clk), .clr(reset));
  Register #(.width(32)) register_30 (.D(in15), .en(WE), .Q(out15), .clk(clk), .clr(reset));
  Register #(.width(32)) register_31 (.D(in23), .en(WE), .Q(out23), .clk(clk), .clr(reset));
  Register #(.width(32)) register_32 (.D(in31), .en(WE), .Q(out31), .clk(clk), .clr(reset));
endmodule

module PC (
  input  [31:0] \input ,
  input  clk,
  input  reset,
  output [31:0] \output 
);

  Register #(.width(32)) register_1 (.D(\input ), .Q(\output ), .clk(clk), .clr(reset));  // open: en
endmodule

module NPC (
  input  [31:0] \input ,
  input  RsignPC,
  input  IsignPC,
  input  JsignPC,
  input  [31:0] NPCrs_R,
  input  [15:0] NPCimm_I,
  input  [31:0] NPCadd_J,
  output [31:0] \output 
);

  wire [31:0] adder_1_out, bit_extender_1_out, multiplexer_1_out, multiplexer_2_out, NPCimm_I32, pc_4;

  Adder #(.width(32)) adder_1 (.a(pc_4), .b(NPCimm_I32), .out(adder_1_out));  // open: cin, cout
  Adder #(.width(32)) adder_2 (.a(\input ), .b(32'h4), .out(pc_4));  // open: cin, cout
  Multiplexer #(.width(32), .enable("false")) multiplexer_1 (
    .in0(pc_4), .in1(adder_1_out), .out(multiplexer_1_out), .sel(IsignPC));
  assign bit_extender_1_out = {{16{NPCimm_I[15]}}, NPCimm_I};  // Bit_Extender bit_extender_1
  Shifter #(.width(32)) shifter_1 (.in(bit_extender_1_out), .\dist (5'b00010), .out(NPCimm_I32));
  Multiplexer #(.width(32), .enable("false")) multiplexer_2 (
    .in0(multiplexer_1_out), .in1(NPCrs_R), .out(multiplexer_2_out), .sel(RsignPC));
  // Probe on NPCimm_I32
  Multiplexer #(.width(32), .enable("false")) multiplexer_3 (
    .in0(multiplexer_2_out), .in1({multiplexer_2_out[31:28], NPCadd_J[25:0], 2'b00}), .out(\output ),
    .sel(JsignPC));

  // Other names for the same wires on the sheet: NPCadd_J_t[25:0] = NPCadd_J[25:0]
endmodule

module IM (
  input  [31:0] PC,
  output [31:0] instr
);

  ROM #(.addrWidth(5), .dataWidth(32)) rom_1 (.addr(PC[6:2]), .data(instr));  // open: sel

  // Notes on the sheet:
  //   contents of rom_1 (hex, n*v repeats v):
  //   34100007 34110007 c000c05 3411000f 8000c09 1611fffb 3412000f 34140001 3e00008
endmodule

module ALU (
  input  [31:0] A,
  input  [31:0] B,
  input  [31:0] DM_RD,
  input  [31:0] Instr,
  output RsignPC,
  output [31:0] Result,
  output IsignPC,
  output JsignPC,
  output DM_WE,
  output [4:0] DM_A,
  output [31:0] Rrs,
  output [31:0] DM_WD,
  output [15:0] limm,
  output [31:0] Jadd,
  output DM_awake
);

  wire and_4_out, and_5_out, and_6_out, and_7_out, and_14_out, and_15_out, and_16_out, and_17_out,
       and_18_out, and_19_out, and_20_out, Bunch, Cal_1, Cal_3, comparator_1_eq, comparator_2_eq,
       comparator_3_eq, comparator_4_eq, comparator_5_eq, comparator_6_eq, comparator_7_eq, comparator_8_eq,
       comparator_9_eq, comparator_10_eq, comparator_11_eq, comparator_12_eq, comparator_13_eq,
       comparator_14_eq, comparator_15_eq, comparator_16_eq, comparator_18_eq, comparator_19_eq,
       comparator_20_eq, comparator_21_eq, comparator_22_eq, equ, Isign, J, Jal, Jsign, Load, not_1_out,
       not_2_out, or_1_out, or_3_out, or_5_out, or_7_out, Rsign;
  wire [3:0] ALUcode;
  wire [4:0] rdR, rsI, rsR, rtI, rtR;
  wire [5:0] funct, opcode, opcodeJ, rsplitter_2_funct;
  wire [15:0] imm16;
  wire [25:0] instr_index;
  wire [31:0] A_B, A_B_t, A_B_t_t, A_B_t_t_t, A_B_t_t_t_t;

  Rsplitter rsplitter_1 (.instr(Instr), .funct(funct), .rd(rdR), .rt(rtR), .rs(rsR));  // open: shamt, opcode
  Isplitter isplitter_1 (.instr(Instr), .imm(imm16), .rt(rtI), .rs(rsI), .opcode(opcode));
  Jsplitter jsplitter_1 (.instr(Instr), .instr_index(instr_index), .opcode(opcodeJ));
  Comparator #(.width(6)) comparator_1 (.a(6'b001000), .b(funct), .eq(comparator_1_eq));  // open: gt, lt
  Rsplitter rsplitter_2 (.instr(Instr), .funct(rsplitter_2_funct));  // open: shamt, rd, rt, rs, opcode
  Adder #(.width(32)) adder_1 (.a(A), .b(B), .out(A_B_t));  // open: cin, cout
  Subtractor #(.width(32)) subtractor_1 (.a(A), .b(B), .out(A_B_t_t));  // open: bin, bout
  not not_1 (not_1_out, comparator_1_eq);
  Comparator #(.width(6)) comparator_2 (.a(6'b001000), .b(rsplitter_2_funct), .eq(comparator_2_eq));  // open: gt, lt
  and and_1 (Cal_3, Rsign, not_1_out);
  and and_2 (RsignPC, Rsign, comparator_2_eq);
  Comparator #(.width(6)) comparator_3 (.a(opcode), .b(6'b001000), .eq(comparator_3_eq));  // open: gt, lt
  or or_1 (or_1_out, comparator_3_eq, comparator_4_eq);
  Comparator #(.width(6)) comparator_4 (.a(opcode), .b(6'b001001), .eq(comparator_4_eq));  // open: gt, lt
  Comparator #(.width(6)) comparator_5 (.a(opcode), .b(6'b001100), .eq(comparator_5_eq));  // open: gt, lt
  Comparator #(.width(6)) comparator_6 (.a(opcode), .b(6'b001101), .eq(comparator_6_eq));  // open: gt, lt
  Comparator #(.width(6)) comparator_7 (.a(opcode), .b(6'b001110), .eq(comparator_7_eq));  // open: gt, lt
  Comparator #(.width(6)) comparator_8 (.a(opcode), .b(6'b001111), .eq(comparator_8_eq));  // open: gt, lt
  Comparator #(.width(6)) comparator_9 (.a(opcode), .b(6'b000100), .eq(comparator_9_eq));  // open: gt, lt
  Comparator #(.width(6)) comparator_10 (.a(opcode), .b(6'b000101), .eq(comparator_10_eq));  // open: gt, lt
  Comparator #(.width(6)) comparator_11 (.a(opcode), .b(6'b101011), .eq(comparator_11_eq));  // open: gt, lt
  Comparator #(.width(6)) comparator_12 (.a(opcode), .b(6'b100011), .eq(comparator_12_eq));  // open: gt, lt
  Comparator #(.width(6)) comparator_13 (.a(opcodeJ), .b(6'b000010), .eq(comparator_13_eq));  // open: gt, lt
  Comparator #(.width(6)) comparator_14 (.a(opcodeJ), .b(6'b000011), .eq(comparator_14_eq));  // open: gt, lt
  assign A_B = A & B;  // AND_Gate and_3, 32 bits wide
  assign A_B_t_t_t_t = A | B;  // OR_Gate or_2, 32 bits wide
  and and_4 (and_4_out, Isign, or_1_out);
  and and_5 (and_5_out, Isign, comparator_5_eq);
  and and_6 (and_6_out, Isign, comparator_6_eq);
  and and_7 (and_7_out, Isign, comparator_7_eq);
  and and_8 (Cal_1, Isign, comparator_8_eq);
  or or_3 (or_3_out, comparator_9_eq, comparator_10_eq);
  and and_9 (DM_WE, Isign, comparator_11_eq);
  and and_10 (Load, Isign, comparator_12_eq);
  and and_11 (J, Jsign, comparator_13_eq);
  and and_12 (Jal, Jsign, comparator_14_eq);
  assign A_B_t_t_t = A ^ B;  // XOR_Gate xor_1, 32 bits wide
  Comparator #(.width(6)) comparator_15 (.a(funct), .b(6'b100100), .eq(comparator_15_eq));  // open: gt, lt
  Comparator #(.width(6)) comparator_16 (.a(funct), .b(6'b100001), .eq(comparator_16_eq));  // open: gt, lt
  Multiplexer #(.width(4), .enable("false")) multiplexer_1 (.in1(4'b0110), .out(ALUcode), .sel(RsignPC));  // open: in0
  Multiplexer #(.width(4), .enable("false")) multiplexer_2 (
    .in1(4'b0010), .out(ALUcode), .sel(and_4_out));  // open: in0
  Multiplexer #(.width(4), .enable("false")) multiplexer_3 (
    .in1(4'b0000), .out(ALUcode), .sel(and_5_out));  // open: in0
  Multiplexer #(.width(4), .enable("false")) multiplexer_4 (
    .in1(4'b0001), .out(ALUcode), .sel(and_6_out));  // open: in0
  Multiplexer #(.width(4), .enable("false")) multiplexer_5 (
    .in1(4'b0100), .out(ALUcode), .sel(and_7_out));  // open: in0
  and and_13 (Bunch, Isign, or_3_out);
  Comparator #(.width(32)) comparator_17 (.a(A), .b(B), .eq(equ));  // open: gt, lt
  // Probe on ALUcode
  and and_14 (and_14_out, Cal_3, comparator_15_eq);
  and and_15 (and_15_out, Cal_3, comparator_16_eq);
  Multiplexer #(.width(4), .enable("false")) multiplexer_6 (.in1(4'b0101), .out(ALUcode), .sel(Cal_1));  // open: in0
  or or_4 (DM_awake, DM_WE, Load);
  Multiplexer #(.select(4), .width(32), .enable("false")) multiplexer_7 (
    .in0(A_B), .in1(A_B_t_t_t_t), .in2(A_B_t), .in3(A_B_t_t), .in4(A_B_t_t_t), .in5(B), .in6(A), .in7(DM_RD),
    .out(Result), .sel(ALUcode));  // open: in8, in9, in10, in11, in12, in13, in14, in15
  Multiplexer #(.width(4), .enable("false")) multiplexer_8 (
    .in1(4'b0000), .out(ALUcode), .sel(and_14_out));  // open: in0
  Multiplexer #(.width(4), .enable("false")) multiplexer_9 (
    .in1(4'b0010), .out(ALUcode), .sel(and_15_out));  // open: in0
  Multiplexer #(.width(4), .enable("false")) multiplexer_10 (
    .in1(4'b0110), .out(ALUcode), .sel(or_5_out));  // open: in0
  or or_5 (or_5_out, J, Jal);
  Comparator #(.width(6)) comparator_18 (.a(opcode), .b(6'b000100), .eq(comparator_18_eq));  // open: gt, lt
  Comparator #(.width(6)) comparator_19 (.a(funct), .b(6'b100101), .eq(comparator_19_eq));  // open: gt, lt
  Comparator #(.width(6)) comparator_20 (.a(funct), .b(6'b100011), .eq(comparator_20_eq));  // open: gt, lt
  Multiplexer #(.width(16), .enable("false")) multiplexer_11 (.in1(imm16), .out(limm), .sel(and_16_out));  // open: in0
  and and_16 (and_16_out, Bunch, equ, comparator_18_eq);
  or or_6 (JsignPC, J, Jal);
  Multiplexer #(.width(4), .enable("false")) multiplexer_12 (
    .in1(4'b0001), .out(ALUcode), .sel(and_17_out));  // open: in0
  and and_17 (and_17_out, Cal_3, comparator_19_eq);
  Multiplexer #(.width(4), .enable("false")) multiplexer_13 (
    .in1(4'b0011), .out(ALUcode), .sel(and_18_out));  // open: in0
  and and_18 (and_18_out, Cal_3, comparator_20_eq);
  Multiplexer #(.width(32), .enable("false")) multiplexer_14 (.in1(Result), .out(Rrs), .sel(RsignPC));  // open: in0
  Multiplexer #(.width(32), .enable("false")) multiplexer_15 (.in0({32{1'b0}}), .in1(B), .out(DM_WD), .sel(DM_WE));
  or or_7 (or_7_out, J, Jal);
  Comparator #(.width(6)) comparator_21 (.a(funct), .b({6{1'b0}}), .eq(comparator_21_eq));  // open: gt, lt
  not not_2 (not_2_out, equ);
  Comparator #(.width(6)) comparator_22 (.a(opcode), .b(6'b000101), .eq(comparator_22_eq));  // open: gt, lt
  Multiplexer #(.width(4), .enable("false")) multiplexer_16 (.in1(4'b0111), .out(ALUcode), .sel(Load));  // open: in0
  Multiplexer #(.width(32), .enable("false")) multiplexer_17 (.in1(B), .out(Jadd), .sel(or_7_out));  // open: in0
  and and_19 (and_19_out, Cal_3, comparator_21_eq);
  Multiplexer #(.width(16), .enable("false")) multiplexer_18 (.in1(imm16), .out(limm), .sel(and_20_out));  // open: in0
  and and_20 (and_20_out, Bunch, not_2_out, comparator_22_eq);
  Multiplexer #(.width(4), .enable("false")) multiplexer_19 (
    .in1(4'b0110), .out(ALUcode), .sel(and_19_out));  // open: in0
  or or_8 (IsignPC, and_20_out, and_16_out);
  Multiplexer #(.width(4), .enable("false")) multiplexer_20 (.in1(4'b0110), .out(ALUcode), .sel(Bunch));  // open: in0
  InstrLog instrlog_1 (.instr(Instr), .Rsign(Rsign), .Isign(Isign), .Jsign(Jsign));  // open: RsignPC, JsignPC, IsignPC

  assign DM_A = A[6:2];

  // Other names for the same wires on the sheet: FromDM[31:0] = DM_RD; Iimm[15:0] = limm; Jr = RsignPC;
  //   luiB[31:0] = B; Store = DM_WE

  // Notes on the sheet:
  //   J类指令
  //   Cal_3为三目运算类，例如add
  //   jr
  //   Jr类指令，跳至寄存器，R型
  //   jr
  //   Cal_2为双目运算类，例如addi
  //   Cal_1为单目运算类，例如lui
  //   Bunch为分支类，例如beq,转NPC
  //   S为存储类，例如sw,转DM
  //   L为读取类，例如lw,转DM
  //   addi
  //   addiu
  //   andi
  //   ori
  //   xori
  //   lui
  //   beq
  //   bne
  //   sw
  //   lw
  //   包括R型非jr的所有
  //   j
  //   jal
  //   and
  //   addu
  //   beq
  //   or
  //   subu
  //   bne
  //   nop
endmodule

module DM (
  input  clk,
  input  reset,
  input  WE,
  input  DM_awake,
  input  [4:0] A,
  input  [31:0] WD,
  output [31:0] RD
);

  wire multiplexer_3_out;
  wire [4:0] multiplexer_1_out;
  wire [31:0] multiplexer_2_out, ram_1_data;

  Multiplexer #(.width(5), .enable("false")) multiplexer_1 (
    .in0({5{1'b0}}), .in1(A), .out(multiplexer_1_out), .sel(DM_awake));
  Multiplexer #(.width(32), .enable("false")) multiplexer_2 (
    .in0({32{1'b0}}), .in1(WD), .out(multiplexer_2_out), .sel(DM_awake));
  Multiplexer #(.enable("false")) multiplexer_3 (.in0(1'b0), .in1(WE), .out(multiplexer_3_out), .sel(DM_awake));
  RAM #(.addrWidth(5), .dataWidth(32), .bus("separate")) ram_1 (
    .addr(multiplexer_1_out), .din(multiplexer_2_out), .data(ram_1_data), .str(multiplexer_3_out), .clk(clk),
    .clr(reset));  // open: sel, ld
  Multiplexer #(.width(32), .enable("false")) multiplexer_4 (
    .in0({32{1'b0}}), .in1(ram_1_data), .out(RD), .sel(DM_awake));
endmodule

module IFU (
  input  clk,
  input  reset,
  input  RsignPC,
  input  IsignPC,
  input  JsignPC,
  input  [31:0] Rrs,
  input  [15:0] Iimm,
  input  [31:0] Jadd,
  output [31:0] instr,
  output [31:0] PC
);

  wire [31:0] npc_1_output;

  PC pc_1 (.clk(clk), .reset(reset), .\output (PC), .\input (npc_1_output));
  NPC npc_1 (
    .\input (PC), .RsignPC(RsignPC), .IsignPC(IsignPC), .JsignPC(JsignPC), .NPCrs_R(Rrs), .NPCimm_I(Iimm),
    .NPCadd_J(Jadd), .\output (npc_1_output));
  IM im_1 (.PC(PC), .instr(instr));
endmodule

module InstrLog (
  input  [31:0] instr,
  output Rsign,
  output Isign,
  output Jsign,
  output RsignPC,
  output IsignPC,
  output JsignPC
);

  wire and_1_out, and_2_out, and_3_out, and_4_out, comparator_1_eq, comparator_2_eq, comparator_3_eq,
       comparator_4_eq, comparator_5_eq, comparator_6_eq, comparator_7_eq, comparator_8_eq, comparator_9_eq,
       comparator_10_eq, comparator_11_eq, nor_1_out, not_2_out, or_1_out, or_2_out;

  or or_1 (or_1_out, instr[26], instr[27], instr[28], instr[29], instr[30], instr[31]);
  nor nor_1 (nor_1_out, instr[28], instr[29], instr[30], instr[31]);
  Comparator #(.width(6)) comparator_1 (.a(instr[31:26]), .b(6'b000100), .eq(comparator_1_eq));  // open: gt, lt
  Comparator #(.width(6)) comparator_2 (.a(instr[31:26]), .b(6'b000001), .eq(comparator_2_eq));  // open: gt, lt
  Comparator #(.width(5)) comparator_3 (.a(instr[20:16]), .b(5'b00001), .eq(comparator_3_eq));  // open: gt, lt
  Comparator #(.width(6)) comparator_4 (.a(instr[31:26]), .b(6'b000111), .eq(comparator_4_eq));  // open: gt, lt
  Comparator #(.width(5)) comparator_5 (.a(instr[20:16]), .b({5{1'b0}}), .eq(comparator_5_eq));  // open: gt, lt
  Comparator #(.width(6)) comparator_6 (.a(instr[31:26]), .b(6'b000110), .eq(comparator_6_eq));  // open: gt, lt
  Comparator #(.width(5)) comparator_7 (.a(instr[20:16]), .b({5{1'b0}}), .eq(comparator_7_eq));  // open: gt, lt
  Comparator #(.width(6)) comparator_8 (.a(instr[31:26]), .b(6'b000001), .eq(comparator_8_eq));  // open: gt, lt
  Comparator #(.width(5)) comparator_9 (.a(instr[20:16]), .b({5{1'b0}}), .eq(comparator_9_eq));  // open: gt, lt
  Comparator #(.width(6)) comparator_10 (.a(instr[31:26]), .b(6'b000101), .eq(comparator_10_eq));  // open: gt, lt
  and and_1 (and_1_out, comparator_2_eq, comparator_3_eq);
  and and_2 (and_2_out, comparator_4_eq, comparator_5_eq);
  and and_3 (and_3_out, comparator_6_eq, comparator_7_eq);
  and and_4 (and_4_out, comparator_8_eq, comparator_9_eq);
  not not_1 (Rsign, or_1_out);
  not not_2 (not_2_out, Jsign);
  and and_5 (Jsign, or_1_out, nor_1_out, instr[27]);
  Comparator #(.width(6)) comparator_11 (.a(instr[5:0]), .b(6'b001000), .eq(comparator_11_eq));  // open: gt, lt
  and and_6 (Isign, or_1_out, not_2_out);
  or or_2 (or_2_out, comparator_1_eq, and_1_out, and_2_out, and_3_out, and_4_out, comparator_10_eq);
  and and_7 (RsignPC, Rsign, comparator_11_eq);
  and and_8 (IsignPC, Isign, or_2_out);

  assign JsignPC = Jsign;

  // Other names for the same wires on the sheet: funct[5:0] = instr[5:0]; rt[4:0] = instr[20:16]
endmodule

// R
module Rsplitter (
  input  [31:0] instr,
  output [5:0] funct,
  output [4:0] shamt,
  output [4:0] rd,
  output [4:0] rt,
  output [4:0] rs,
  output [5:0] opcode
);


  assign funct = instr[5:0];
  assign opcode = instr[31:26];
  assign rd = instr[15:11];
  assign rs = instr[25:21];
  assign rt = instr[20:16];
  assign shamt = instr[10:6];
endmodule

// I
module Isplitter (
  input  [31:0] instr,
  output [15:0] imm,
  output [4:0] rt,
  output [4:0] rs,
  output [5:0] opcode
);


  assign imm = instr[15:0];
  assign opcode = instr[31:26];
  assign rs = instr[25:21];
  assign rt = instr[20:16];
endmodule

// J
module Jsplitter (
  input  [31:0] instr,
  output [25:0] instr_index,
  output [5:0] opcode
);


  assign instr_index = instr[25:0];
  assign opcode = instr[31:26];
endmodule

// RFC
module RF_controller (
  input  clk,
  input  reset,
  input  [31:0] Instr,
  input  [31:0] WD,
  input  [31:0] PC,
  output [31:0] RD1,
  output [31:0] RD2,
  output RF_WE,
  output [4:0] RF_Add
);

  wire Bunch, Cal_1, Cal_2, Cal_3, comparator_1_eq, comparator_2_eq, comparator_3_eq, comparator_4_eq,
       comparator_5_eq, comparator_6_eq, comparator_7_eq, comparator_8_eq, comparator_9_eq, comparator_10_eq,
       comparator_11_eq, comparator_12_eq, comparator_13_eq, comparator_14_eq, comparator_15_eq, Isign, J,
       Jal, Jr, Jsign, Load, not_1_out, or_1_out, or_2_out, Rsign, Store;
  wire [4:0] A1, A2, rdR, rsI, rsR, rtI, rtR;
  wire [5:0] opcode, opcodeJ, rsplitter_1_funct, rsplitter_2_funct;
  wire [15:0] imm16;
  wire [25:0] instr_index;
  wire [31:0] adder_2_out, bit_extender_1_out, bit_extender_2_out, bit_extender_3_out, bit_extender_4_out,
       bit_extender_5_out, imm32, multiplexer_28_out, RD1_t, RD1plus, RD2_t;

  Rsplitter rsplitter_1 (
    .instr(Instr), .funct(rsplitter_1_funct), .rd(rdR), .rt(rtR), .rs(rsR));  // open: shamt, opcode
  Rsplitter rsplitter_2 (.instr(Instr), .funct(rsplitter_2_funct));  // open: shamt, rd, rt, rs, opcode
  Isplitter isplitter_1 (.instr(Instr), .imm(imm16), .rt(rtI), .rs(rsI), .opcode(opcode));
  Comparator #(.width(6)) comparator_1 (.a(6'b001000), .b(rsplitter_1_funct), .eq(comparator_1_eq));  // open: gt, lt
  not not_1 (not_1_out, comparator_1_eq);
  Comparator #(.width(6)) comparator_2 (.a(6'b001000), .b(rsplitter_2_funct), .eq(comparator_2_eq));  // open: gt, lt
  Jsplitter jsplitter_1 (.instr(Instr), .instr_index(instr_index), .opcode(opcodeJ));
  and and_1 (Cal_3, Rsign, not_1_out);
  and and_2 (Jr, Rsign, comparator_2_eq);
  Comparator #(.width(6)) comparator_3 (.a(opcode), .b(6'b001000), .eq(comparator_3_eq));  // open: gt, lt
  Comparator #(.width(6)) comparator_4 (.a(opcode), .b(6'b001001), .eq(comparator_4_eq));  // open: gt, lt
  Comparator #(.width(6)) comparator_5 (.a(opcode), .b(6'b001100), .eq(comparator_5_eq));  // open: gt, lt
  Comparator #(.width(6)) comparator_6 (.a(opcode), .b(6'b001101), .eq(comparator_6_eq));  // open: gt, lt
  Comparator #(.width(6)) comparator_7 (.a(opcode), .b(6'b001110), .eq(comparator_7_eq));  // open: gt, lt
  Comparator #(.width(6)) comparator_8 (.a(opcode), .b(6'b001111), .eq(comparator_8_eq));  // open: gt, lt
  Comparator #(.width(6)) comparator_9 (.a(opcode), .b(6'b000100), .eq(comparator_9_eq));  // open: gt, lt
  Comparator #(.width(6)) comparator_10 (.a(opcode), .b(6'b000101), .eq(comparator_10_eq));  // open: gt, lt
  Comparator #(.width(6)) comparator_11 (.a(opcode), .b(6'b101011), .eq(comparator_11_eq));  // open: gt, lt
  Comparator #(.width(6)) comparator_12 (.a(opcode), .b(6'b100011), .eq(comparator_12_eq));  // open: gt, lt
  RF rf_1 (.A1(A1), .A2(A2), .A3(RF_Add), .WD(WD), .clk(clk), .reset(reset), .WE(RF_WE), .RD1(RD1_t), .RD2(RD2_t));
  Multiplexer #(.width(5), .enable("false")) multiplexer_1 (.in1(rsR), .out(A1), .sel(Cal_3));  // open: in0
  Multiplexer #(.width(5), .enable("false")) multiplexer_2 (.in1(rtR), .out(A2), .sel(Cal_3));  // open: in0
  Multiplexer #(.width(5), .enable("false")) multiplexer_3 (.in1(rdR), .out(RF_Add), .sel(Cal_3));  // open: in0
  Multiplexer #(.width(5), .enable("false")) multiplexer_4 (.in1(rsR), .out(A1), .sel(Jr));  // open: in0
  and and_3 (Cal_1, Isign, comparator_8_eq);
  or or_1 (or_1_out, comparator_9_eq, comparator_10_eq);
  and and_4 (Store, Isign, comparator_11_eq);
  and and_5 (Load, Isign, comparator_12_eq);
  Comparator #(.width(6)) comparator_13 (.a(opcodeJ), .b(6'b000010), .eq(comparator_13_eq));  // open: gt, lt
  Comparator #(.width(6)) comparator_14 (.a(opcodeJ), .b(6'b000011), .eq(comparator_14_eq));  // open: gt, lt
  and and_6 (Cal_2, Isign, or_2_out);
  or or_2 (or_2_out, comparator_3_eq, comparator_4_eq, comparator_5_eq, comparator_6_eq, comparator_7_eq);
  and and_7 (Bunch, Isign, or_1_out);
  and and_8 (J, Jsign, comparator_13_eq);
  and and_9 (Jal, Jsign, comparator_14_eq);
  Multiplexer #(.width(32), .enable("false")) multiplexer_5 (.in1(RD1_t), .out(RD1), .sel(Cal_3));  // open: in0
  Multiplexer #(.width(32), .enable("false")) multiplexer_6 (.in1(RD2_t), .out(RD2), .sel(Cal_3));  // open: in0
  Multiplexer #(.width(32), .enable("false")) multiplexer_7 (.in1(RD1_t), .out(RD1), .sel(Jr));  // open: in0
  Multiplexer #(.width(32), .enable("false")) multiplexer_8 (.in1({32{1'b0}}), .out(RD2), .sel(Jr));  // open: in0
  Multiplexer #(.width(5), .enable("false")) multiplexer_9 (.in1(rsI), .out(A1), .sel(Cal_2));  // open: in0
  Multiplexer #(.width(5), .enable("false")) multiplexer_10 (.in1(rtI), .out(RF_Add), .sel(Cal_2));  // open: in0
  Multiplexer #(.width(5), .enable("false")) multiplexer_11 (.in1(rtI), .out(RF_Add), .sel(Cal_1));  // open: in0
  Multiplexer #(.width(5), .enable("false")) multiplexer_12 (.in1(rsI), .out(A1), .sel(Bunch));  // open: in0
  Multiplexer #(.width(5), .enable("false")) multiplexer_13 (.in1(rtI), .out(A2), .sel(Bunch));  // open: in0
  Multiplexer #(.width(5), .enable("false")) multiplexer_14 (.in1({5{1'b0}}), .out(RF_Add), .sel(Bunch));  // open: in0
  Multiplexer #(.width(5), .enable("false")) multiplexer_15 (.in1(rsI), .out(A1), .sel(Store));  // open: in0
  Multiplexer #(.width(5), .enable("false")) multiplexer_16 (.in1(rtI), .out(A2), .sel(Store));  // open: in0
  Multiplexer #(.width(5), .enable("false")) multiplexer_17 (.in1({5{1'b0}}), .out(RF_Add), .sel(Store));  // open: in0
  Multiplexer #(.width(5), .enable("false")) multiplexer_18 (.in1(rsI), .out(A1), .sel(Load));  // open: in0
  Multiplexer #(.width(5), .enable("false")) multiplexer_19 (.in1(rtI), .out(RF_Add), .sel(Load));  // open: in0
  assign bit_extender_1_out = {{6{1'b0}}, instr_index};  // Bit_Extender bit_extender_1
  assign bit_extender_2_out = {{16{1'b0}}, imm16};  // Bit_Extender bit_extender_2
  assign bit_extender_3_out = {{16{imm16[15]}}, imm16};  // Bit_Extender bit_extender_3
  Multiplexer #(.width(32), .enable("false")) multiplexer_20 (.in1(RD1_t), .out(RD1), .sel(Bunch));  // open: in0
  Multiplexer #(.width(32), .enable("false")) multiplexer_21 (.in1(RD2_t), .out(RD2), .sel(Bunch));  // open: in0
  Multiplexer #(.width(32), .enable("false")) multiplexer_22 (.in1(RD1plus), .out(RD1), .sel(Store));  // open: in0
  Multiplexer #(.width(32), .enable("false")) multiplexer_23 (.in1(RD2_t), .out(RD2), .sel(Store));  // open: in0
  Multiplexer #(.width(32), .enable("false")) multiplexer_24 (.in1(RD1plus), .out(RD1), .sel(Load));  // open: in0
  Multiplexer #(.width(32), .enable("false")) multiplexer_25 (.in1({32{1'b0}}), .out(RD2), .sel(Load));  // open: in0
  Multiplexer #(.width(32), .enable("false")) multiplexer_26 (.in1({32{1'b0}}), .out(RD1), .sel(J));  // open: in0
  Multiplexer #(.width(32), .enable("false")) multiplexer_27 (
    .in1(bit_extender_1_out), .out(RD2), .sel(J));  // open: in0
  Multiplexer #(.width(32), .enable("false")) multiplexer_28 (
    .in0(bit_extender_2_out), .in1(bit_extender_3_out), .out(multiplexer_28_out), .sel(comparator_15_eq));
  Comparator #(.width(6)) comparator_15 (.a(opcode), .b(6'b001000), .eq(comparator_15_eq));  // open: gt, lt
  Multiplexer #(.width(32), .enable("false")) multiplexer_29 (
    .in1({imm16, {16{1'b0}}}), .out(imm32), .sel(Cal_1));  // open: in0
  Multiplexer #(.width(32), .enable("false")) multiplexer_30 (
    .in1(multiplexer_28_out), .out(imm32), .sel(Cal_2));  // open: in0
  assign bit_extender_4_out = {{16{imm16[15]}}, imm16};  // Bit_Extender bit_extender_4
  or or_3 (RF_WE, Cal_3, Cal_2, Cal_1, Load, Jal);
  Multiplexer #(.width(32), .enable("false")) multiplexer_31 (.in1(RD1_t), .out(RD1), .sel(Cal_2));  // open: in0
  Multiplexer #(.width(32), .enable("false")) multiplexer_32 (.in1(imm32), .out(RD2), .sel(Cal_2));  // open: in0
  Multiplexer #(.width(32), .enable("false")) multiplexer_33 (.in1({32{1'b0}}), .out(RD1), .sel(Cal_1));  // open: in0
  Multiplexer #(.width(32), .enable("false")) multiplexer_34 (.in1(imm32), .out(RD2), .sel(Cal_1));  // open: in0
  Adder #(.width(32)) adder_1 (.a(bit_extender_4_out), .b(RD1_t), .out(RD1plus));  // open: cin, cout
  Multiplexer #(.width(5), .enable("false")) multiplexer_35 (.in1({5{1'b1}}), .out(RF_Add), .sel(Jal));  // open: in0
  InstrLog instrlog_1 (.instr(Instr), .Rsign(Rsign), .Isign(Isign), .Jsign(Jsign));  // open: RsignPC, JsignPC, IsignPC
  Multiplexer #(.width(32), .enable("false")) multiplexer_36 (.in1(adder_2_out), .out(RD1), .sel(Jal));  // open: in0
  Adder #(.width(32)) adder_2 (.a(PC), .b(32'h4), .out(adder_2_out));  // open: cin, cout
  Multiplexer #(.width(32), .enable("false")) multiplexer_37 (
    .in1(bit_extender_5_out), .out(RD2), .sel(Jal));  // open: in0
  assign bit_extender_5_out = {{6{1'b0}}, instr_index};  // Bit_Extender bit_extender_5

  // Other names for the same wires on the sheet: A3[4:0] = RF_Add; Out1[31:0] = RD1; Out2[31:0] = RD2; WE = RF_WE

  // Notes on the sheet:
  //   jr
  //   jr
  //   Cal_3为三目运算类，例如add
  //   Jr类指令，跳至寄存器，R型
  //   Cal_2为双目运算类，例如addi
  //   Cal_1为单目运算类，例如lui
  //   Bunch为分支类，例如beq
  //   S为存储类，例如sw
  //   L为读取类，例如lw
  //   J类指令
  //   addi
  //   addiu
  //   andi
  //   ori
  //   xori
  //   lui
  //   beq
  //   bne
  //   sw
  //   lw
  //   包括R型非jr的所有
  //   j
  //   jal
  //   addi
endmodule
